# Fritzing sketch DO_NHIET_DO (saved by Fritzing 0.9.2b)
circuit board: 7.32796cm x 6.19189cm
breadboards: 1

parts:
  NODE-MCU-8266 = ESP8266 NodeMCU LoLin module
  J1 = Power Jack [package=power_jack_slot]
  DHT1 = DHT22 Humidity and Temperature Sensor
  YL-83_-_Control_Board1 = YL-83 Rain Sensor - Control Board  # not connected
  J3 = female pin header, 2 pins [form="♀ (female)"]
  J4 = female pin header, 2 pins [form="♀ (female)"]
  YL-83-4PIN = female pin header, 4 pins [form="♀ (female)"]
  J5 = female pin header, 15 pins [form="♀ (female)"]
  J6 = female pin header, 15 pins [form="♀ (female)"]
  J7 = female pin header, 2 pins [form="♀ (female)"]
  J8 = female pin header, 2 pins [form="♀ (female)"]
  J9 = female pin header, 2 pins [form="♀ (female)"]
  J10 = female pin header, 2 pins [form="♀ (female)"]
  J11 = female pin header, 2 pins [form="♀ (female)"]
  J12 = female pin header, 2 pins [form="♀ (female)"]
  LED1 = LED - 5mm [color="Red (633nm)" package="5 mm [THT]"]
  R1 = Resistor [tolerance=±5% resistance=220 package=THT]
  U3 = Voltage Regulator - 5V [package="TO220 [THT]"]
  U2 = Voltage Regulator LM1117 [package=sot223]

nets:
  N1: NODE-MCU-8266.D0, J6.pin1
  N2: NODE-MCU-8266.D1, J6.pin2
  N3: NODE-MCU-8266.D2, DHT1.DATA, J6.pin3
  N4: NODE-MCU-8266.D3, J6.pin4
  N5: NODE-MCU-8266.D4, J6.pin5
  3V3: NODE-MCU-8266.3V3, DHT1.VDD, YL-83-4PIN.pin4, J5.pin11, J6.pin6, J6.pin15
  GND: NODE-MCU-8266.GND, J1.GND, DHT1.GND, YL-83-4PIN.pin3, J5.pin2, J5.pin10, J5.pin14, J6.pin7, J6.pin14, J10.pin2, J11.pin2, J12.pin2, LED1.cathode, U3.GND, U2.ADJ
  N6: NODE-MCU-8266.D5, J6.pin8
  N7: NODE-MCU-8266.D6, J6.pin9
  N8: NODE-MCU-8266.D7, J6.pin10
  N9: NODE-MCU-8266.D8, J6.pin11
  N10: NODE-MCU-8266.RX, J6.pin12
  N11: NODE-MCU-8266.TX, J6.pin13
  N12: NODE-MCU-8266.Vin, J5.pin15, J10.pin1, J11.pin1, J12.pin1, U2.OUT
  N13: NODE-MCU-8266.RST, J5.pin13
  N14: NODE-MCU-8266.EN, J5.pin12
  N15: NODE-MCU-8266.SK, J5.pin9
  N16: NODE-MCU-8266.S0, J5.pin8
  N17: NODE-MCU-8266.SC, J5.pin7
  N18: NODE-MCU-8266.S1, J5.pin6
  N19: NODE-MCU-8266.S2, J5.pin5
  N20: NODE-MCU-8266.S3, J5.pin4
  N21: NODE-MCU-8266.VU, J5.pin3
  N22: NODE-MCU-8266.A0, YL-83-4PIN.pin1, J5.pin1
  N23: J1.PWR, U3.input_voltage, U2.IN
  N24: J3.pin1, J4.pin1
  N25: J3.pin2, J4.pin2
  N26: J7.pin1, J8.pin1, J9.pin1
  N27: J7.pin2, J8.pin2, J9.pin2, R1.Pin_0, U3.output_voltage
  N28: LED1.anode, R1.Pin_1

custom parts:
  ESP8266 NodeMCU LoLin module: ESP8266 based NodeMCU
  YL-83 Rain Sensor - Control Board: The YL-83 is a rain sensor that has more resistance when dry and less resistance when wet. The module runs at 5V.
