# Fritzing sketch MY_PROJECT (saved by Fritzing 0.9.2b)
circuit board: 8.46528cm x 6.51482cm
breadboards: 1

parts:
  DHT1 = DHT22 Humidity and Temperature Sensor
  U4 = ESP8266 NodeMCU LoLin module
  GND = female pin header, 4 pins [form="♀ (female)"]
  GND_2 = female pin header, 4 pins [form="♀ (female)"]
  3_3V = female pin header, 4 pins [form="♀ (female)"]
  5V = female pin header, 4 pins [form="♀ (female)"]
  J1 = female pin header, 15 pins [form="♀ (female)"]
  J2 = female pin header, 15 pins [form="♀ (female)"]
  microSD1 = MicroSD Card Module
  J3 = Generic female header - 3 pins [form="♀ (female)" package=THT]
  R1 = Resistor [tolerance=±5% resistance=220 package=THT]
  LED1 = LED - 5mm [color="Red (633nm)" package="5 mm [THT]"]
  J5 = Generic female header - 4 pins [form="♀ (female)" package=THT]
  IR_TX = female pin header, 2 pins [form="♀ (female)"]
  IR_RX = female pin header, 3 pins [form="♀ (female)"]

nets:
  3.3V: DHT1.VDD, U4.3V3, 3_3V.pin1, 3_3V.pin2, 3_3V.pin3, 3_3V.pin4, J1.pin11, J2.pin6, J2.pin15, IR_RX.pin3
  D1: DHT1.DATA, U4.D1, J2.pin2
  GND: DHT1.GND, U4.GND, GND.pin1, GND.pin2, GND.pin3, GND.pin4, GND_2.pin1, GND_2.pin2, GND_2.pin3, GND_2.pin4, J1.pin2, J1.pin10, J1.pin14, J2.pin7, J2.pin14, microSD1.GND, J3.GND, LED1.cathode, J5.GND, IR_TX.pin1, IR_RX.pin2
  N1: U4.D0, J2.pin1
  D2: U4.D2, J2.pin3, J3.DATA
  D3: U4.D3, J2.pin4, J5.DATA2
  N2: U4.D4, J2.pin5
  D5: U4.D5, J2.pin8, microSD1.SCK
  D6: U4.D6, J2.pin9, microSD1.MISO
  D7: U4.D7, J2.pin10, microSD1.MOSI
  D8: U4.D8, J2.pin11, microSD1.CS
  N3: U4.RX, J2.pin12
  N4: U4.TX, J2.pin13
  VCC: U4.Vin, 5V.pin1, 5V.pin2, 5V.pin3, 5V.pin4, J1.pin15, J3.VCC, R1.Pin_1, J5.VCC
  N5: U4.RST, J1.pin13
  N6: U4.EN, J1.pin12
  N7: U4.SK, J1.pin9
  N8: U4.S0, J1.pin8
  N9: U4.SC, J1.pin7
  N10: U4.S1, J1.pin6
  N11: U4.S2, J1.pin5, IR_TX.pin2
  N12: U4.S3, J1.pin4, IR_RX.pin1
  N13: U4.VU, J1.pin3
  N14: U4.A0, J1.pin1
  N15: R1.Pin_0, LED1.anode

custom parts:
  ESP8266 NodeMCU LoLin module: ESP8266 based NodeMCU
  MicroSD Card Module: A common microSD card module.
  Generic female header - 3 pins: Generic female header
  Generic female header - 4 pins: Generic female header
